// Logisim project lab1.circ as structural Verilog: 1 circuit, main circuit main
module main (
  input  in_1,
  input  in_2,
  input  in_3,
  input  in_4,
  input  in_5,
  input  in_6,
  input  in_7,
  input  in_8,
  input  in_9,
  output out_10,
  output out_11,
  output out_12
);

  wire and_1_out, and_2_out, n7404_1_p2, n7404_2_p2, n7408_1_p3, n7408_2_p3, n7408_3_p3, n7408_3_p6,
       not_1_out;

  // _7404 7404_1: pin names not known; wires that end beside it: in_5, n7404_1_p2
  // _7404 7404_2: pin names not known; wires that end beside it: in_8, n7404_2_p2
  not not_1 (not_1_out, in_2);
  and and_1 (and_1_out, in_1, not_1_out);
  and and_2 (and_2_out, in_2, in_3);
  // _7408 7408_1: pin names not known; wires that end beside it: in_4, n7404_1_p2, n7408_1_p3
  // _7408 7408_2: pin names not known; wires that end beside it: in_6, in_5, n7408_2_p3
  // _7408 7408_3: pin names not known; wires that end beside it: in_7, n7404_2_p2, n7408_3_p3, in_9, in_8, n7408_3_p6
  or or_1 (out_10, and_1_out, and_2_out);
  // _7432 7432_1: pin names not known; wires that end beside it: n7408_1_p3, n7408_2_p3, out_11
  // _7432 7432_2: pin names not known; wires that end beside it: n7408_3_p3, n7408_3_p6, out_12
endmodule
