// Logisim project lab1p2.circ as structural Verilog: 1 circuit, main circuit main
module main (
  input  in_1,
  input  in_2,
  input  in_3,
  input  in_4,
  output out_5
);

  wire n7404_1_p2, n7404_1_p4, n7404_1_p5, n7404_1_p8;

  // _7404 7404_1: pin names not known; wires that end beside it: in_2, n7404_1_p2, in_3, n7404_1_p4, n7404_1_p5, n7404_1_p4, in_1, n7404_1_p8
  // _7408 7408_1: pin names not known; wires that end beside it: in_4, n7404_1_p2
  // _7432 7432_1: pin names not known; wires that end beside it: n7404_1_p5, n7404_1_p8, out_5
endmodule
